# Fritzing sketch Hardware (saved by Fritzing 0.9.3b)
breadboards: 1

parts:
  J3 = Basic Servo
  VCC1 = 4 x AAA Battery Mount
  Mod1 = Raspberry Pi 4B
  PWM1 = PCA9685 16x12-bit PWM Breakout
  J4 = Basic Servo
  J5 = Basic Servo

nets:
  GND: J3.gnd, VCC1.-, Mod1.GND, PWM1.no_name_yet#501, PWM1.no_name_yet#701, PWM1.no_name_yet#1003, PWM1.no_name_yet#1008, PWM1.no_name_yet#1012, J4.gnd
  VCC: J3.vcc, PWM1.no_name_yet#103, PWM1.no_name_yet#108, PWM1.no_name_yet#112, J4.vcc, J5.vcc
  N1: J3.pulse, PWM1.no_name_yet#12
  N2: Mod1.3V3, PWM1.no_name_yet#505
  N3: Mod1.GPIO2, PWM1.no_name_yet#504
  N4: Mod1.GPIO3, PWM1.no_name_yet#503
  N5: PWM1.no_name_yet#3, J4.pulse
  N6: PWM1.no_name_yet#8, J5.pulse
